// Logisim project projeto3.circ as structural Verilog: 1 circuit, main circuit main
module main (
);

  wire button_1_out, clock_1_out, decoder_1_out0, decoder_1_out1, decoder_1_out2, decoder_1_out3,
       decoder_1_out4, decoder_1_out5, decoder_1_out6, decoder_1_out7;
  wire [2:0] adder_4_out, adder_5_out, adder_6_out;
  wire [7:0] adder_1_out, register_1_q;
  wire [15:0] adder_2_out, adder_3_out, bit_extender_1_out, multiplexer_1_out, multiplexer_2_out,
       multiplexer_3_out, multiplexer_4_out, multiplexer_5_out, multiplexer_6_out, multiplexer_7_out,
       multiplexer_8_out, multiplexer_9_out, multiplexer_10_out, multiplexer_11_out, multiplier_1_out,
       multiplier_2_out, register_2_q, register_3_q, register_4_q, register_5_q, register_6_q, register_7_q,
       register_8_q, register_9_q, rom_1_data;

  Adder adder_1 (.a(register_1_q), .b({8{1'b0}}), .out(adder_1_out), .cin(1'b1));  // open: cout
  Clock clock_1 (.out(clock_1_out));
  Register register_1 (.D(adder_1_out), .clk(clock_1_out), .Q(register_1_q), .clr(button_1_out));  // open: en
  ROM #(.dataWidth(16)) rom_1 (.addr(register_1_q), .data(rom_1_data));
  Button button_1 (.out(button_1_out));
  Multiplexer #(.width(16)) multiplexer_1 (
    .in0(multiplexer_11_out), .in1(multiplexer_10_out), .out(multiplexer_1_out), .sel(rom_1_data[10]));
  Multiplexer #(.width(16)) multiplexer_2 (
    .in0(multiplexer_9_out), .in1(multiplexer_8_out), .out(multiplexer_2_out), .sel(rom_1_data[10]));
  Multiplexer #(.width(16)) multiplexer_3 (
    .in0(multiplexer_7_out), .in1(adder_3_out), .out(multiplexer_3_out), .sel(rom_1_data[11]));
  Multiplier #(.width(16)) multiplier_1 (
    .a(multiplexer_1_out), .b(multiplexer_7_out), .out(multiplier_1_out));  // open: cin, cout
  Multiplier #(.width(16)) multiplier_2 (
    .a(multiplexer_2_out), .b(multiplexer_6_out), .out(multiplier_2_out));  // open: cin, cout
  Adder #(.width(16)) adder_2 (.a(multiplexer_3_out), .b(multiplexer_10_out), .out(adder_2_out));  // open: cin, cout
  Adder #(.width(16)) adder_3 (.a(multiplier_1_out), .b(multiplier_2_out), .out(adder_3_out));  // open: cin, cout
  assign bit_extender_1_out = {{4{rom_1_data[11]}}, rom_1_data[11:0]};  // Bit_Extender bit_extender_1
  Multiplexer #(.width(16)) multiplexer_4 (
    .in0(adder_2_out), .in1(adder_3_out), .out(multiplexer_4_out), .sel(rom_1_data[10]));
  Decoder #(.select(3)) decoder_1 (
    .out0(decoder_1_out0), .out1(decoder_1_out1), .out2(decoder_1_out2), .out3(decoder_1_out3),
    .out4(decoder_1_out4), .out5(decoder_1_out5), .out6(decoder_1_out6), .out7(decoder_1_out7),
    .sel(rom_1_data[15:13]));  // open: en
  Multiplexer #(.width(16)) multiplexer_5 (
    .in0(bit_extender_1_out), .in1(multiplexer_4_out), .out(multiplexer_5_out), .sel(rom_1_data[12]));
  Multiplexer #(.select(3), .width(16)) multiplexer_6 (
    .in0(register_9_q), .in1(register_8_q), .in2(register_7_q), .in3(register_6_q), .in4(register_5_q),
    .in5(register_4_q), .in6(register_3_q), .in7(register_2_q), .out(multiplexer_6_out), .sel(adder_5_out));
  Register #(.width(16)) register_2 (
    .D(multiplexer_5_out), .en(decoder_1_out7), .Q(register_2_q), .clk(clock_1_out), .clr(button_1_out));
  Register #(.width(16)) register_3 (
    .D(multiplexer_5_out), .en(decoder_1_out6), .Q(register_3_q), .clk(clock_1_out), .clr(button_1_out));
  Multiplexer #(.select(3), .width(16)) multiplexer_7 (
    .in0(register_9_q), .in1(register_8_q), .in2(register_7_q), .in3(register_6_q), .in4(register_5_q),
    .in5(register_4_q), .in6(register_3_q), .in7(register_2_q), .out(multiplexer_7_out), .sel(rom_1_data[9:7]));
  Register #(.width(16)) register_4 (
    .D(multiplexer_5_out), .en(decoder_1_out5), .Q(register_4_q), .clk(clock_1_out), .clr(button_1_out));
  Register #(.width(16)) register_5 (
    .D(multiplexer_5_out), .en(decoder_1_out4), .Q(register_5_q), .clk(clock_1_out), .clr(button_1_out));
  Multiplexer #(.select(3), .width(16)) multiplexer_8 (
    .in0(register_9_q), .in1(register_8_q), .in2(register_7_q), .in3(register_6_q), .in4(register_5_q),
    .in5(register_4_q), .in6(register_3_q), .in7(register_2_q), .out(multiplexer_8_out), .sel(adder_4_out));
  Register #(.width(16)) register_6 (
    .D(multiplexer_5_out), .en(decoder_1_out3), .Q(register_6_q), .clk(clock_1_out), .clr(button_1_out));
  Multiplexer #(.select(3), .width(16)) multiplexer_9 (
    .in0(register_9_q), .in1(register_8_q), .in2(register_7_q), .in3(register_6_q), .in4(register_5_q),
    .in5(register_4_q), .in6(register_3_q), .in7(register_2_q), .out(multiplexer_9_out), .sel(adder_6_out));
  Register #(.width(16)) register_7 (
    .D(multiplexer_5_out), .en(decoder_1_out2), .Q(register_7_q), .clk(clock_1_out), .clr(button_1_out));
  Register #(.width(16)) register_8 (
    .D(multiplexer_5_out), .en(decoder_1_out1), .Q(register_8_q), .clk(clock_1_out), .clr(button_1_out));
  Multiplexer #(.select(3), .width(16)) multiplexer_10 (
    .in0(register_9_q), .in1(register_8_q), .in2(register_7_q), .in3(register_6_q), .in4(register_5_q),
    .in5(register_4_q), .in6(register_3_q), .in7(register_2_q), .out(multiplexer_10_out),
    .sel(rom_1_data[15:13]));
  Register #(.width(16)) register_9 (
    .D(multiplexer_5_out), .en(decoder_1_out0), .Q(register_9_q), .clk(clock_1_out), .clr(button_1_out));
  Multiplexer #(.select(3), .width(16)) multiplexer_11 (
    .in0(register_9_q), .in1(register_8_q), .in2(register_7_q), .in3(register_6_q), .in4(register_5_q),
    .in5(register_4_q), .in6(register_3_q), .in7(register_2_q), .out(multiplexer_11_out),
    .sel(rom_1_data[6:4]));
  Adder #(.width(3)) adder_4 (.a(rom_1_data[15:13]), .b(3'b000), .out(adder_4_out), .cin(1'b1));  // open: cout
  Adder #(.width(3)) adder_5 (.a(rom_1_data[9:7]), .b(3'b000), .out(adder_5_out), .cin(1'b1));  // open: cout
  Adder #(.width(3)) adder_6 (.a(rom_1_data[6:4]), .b(3'b000), .out(adder_6_out), .cin(1'b1));  // open: cout

  // Notes on the sheet:
  //   relógio
  //   Registo Contador
  //   contents of rom_1 (hex, n*v repeats v):
  //   2 2003 4004 6002 8001 a005 c002 e002 7080 1500 1a60
  //   reset
  //   ROM
  //   imm (9:7) /       rs1
  //   imm (3:0) /     funct4
  //   imm (11:10) / opcode (11:10) 
  //   rd
  //   imm (6:4) / rs2 / funct3
  //   opcode (12)
  //   se bit 11 = 0 -> +rs1 (add)
  //   se bit 11 = 1 -> +dot (dota)
  //   se bit 10 = 0 -> rs2 (dota)
  //   se bit 10 = 1 -> rd (dot)
  //   rd
  //   rs2 +1 
  //   rd + 1
  //   (bit 10)
  //   (bit 11)
  //   rs1
  //   dota
  //   rs2 
  //   rd
  //   rs1
  //   rs1 + 1
  //   add/dota
  //   dot
  //   imm
  //   add/dot/dota
  //   li
  //   R7
  //   rs1 + 1
  //   R6
  //   rs1
  //   R5
  //   BANCO DE REGISTOS
  //   R4
  //   rd + 1
  //   R3
  //   rs2 + 1
  //   R2
  //   R1
  //   rd
  //   R0
  //   rs2
  //   rd
  //   rs1
  //   rs2
  //   rd + 1
  //   rd
  //   rs1+1
  //   rs1
  //   rs2+1
  //   rs2
endmodule
